// Logisim project lab1.circ as structural Verilog: 1 circuit, main circuit main
module main (
);

  wire Decrease_Temp_out, Increase_Temp_out, n74193_1_pin1, nor_1_out, nor_2_out, not_1_out,
       Start_Heating_out, Stop_Heating_out;
  wire [3:0] n74193_1_pin3;
  wire [6:0] rom_1_data;

  LED Status_LED (.in(not_1_out));
  Button Start_Heating (.out(Start_Heating_out));
  Button Stop_Heating (.out(Stop_Heating_out));
  nor nor_1 (nor_1_out, Stop_Heating_out, nor_2_out);
  nor nor_2 (nor_2_out, nor_1_out, Start_Heating_out);
  not not_1 (not_1_out, nor_2_out);
  Button #(.press("passive")) Increase_Temp (.out(Increase_Temp_out));
  Button #(.press("passive")) Decrease_Temp (.out(Decrease_Temp_out));
  LED led_1 (.in(rom_1_data[5]));
  LED led_2 (.in(rom_1_data[4]));
  LED led_3 (.in(rom_1_data[3]));
  LED led_4 (.in(rom_1_data[2]));
  LED led_5 (.in(rom_1_data[1]));
  LED led_6 (.in(rom_1_data[0]));
  _74193 #(.ShowInternalStructure("true")) u_74193_1 (
    .pin1(n74193_1_pin1), .pin2(n74193_1_pin3[1]), .pin3(n74193_1_pin3[0]), .pin4(Decrease_Temp_out),
    .pin5(Increase_Temp_out), .pin6(n74193_1_pin3[2]), .pin7(n74193_1_pin3[3]), .pin15(n74193_1_pin1),
    .pin14(rom_1_data[6]), .pin11(nor_1_out), .pin10(n74193_1_pin1), .pin9(n74193_1_pin1));  // open: pin13, pin12
  ROM #(.addrWidth(4), .dataWidth(7)) rom_1 (.addr(n74193_1_pin3), .data(rom_1_data));
  // also tied to GND on the sheet: n74193_1_pin1

  // Notes on the sheet:
  //   180
  //   170
  //   160
  //   150
  //   140
  //   130
  //   120
  //   110
  //   100
  //   90
  //   80
  //   contents of rom_1 (hex, n*v repeats v):
  //   0 1 3 2 6 4 c 8 18 10 30 20 40
endmodule
